// Logisim project hkcpu.circ as structural Verilog
module alu (
  input  CLK,
  input  RST,
  input  [15:0] A,
  input  [15:0] B,
  input  [2:0] ALM,
  input  ALO,
  output [2:0] FLG,
  output [15:0] BUS_O
);

  wire and_1_out;
  wire [2:0] comparator_1_gt;
  wire [15:0] adder_1_out, divider_1_out, multiplier_1_out, subtractor_1_out;

  Comparator #(.mode("unsigned"), .width(16)) comparator_1 (
    .a(A), .b(B), .gt(comparator_1_gt[0]), .eq(comparator_1_gt[1]), .lt(comparator_1_gt[2]));
  Adder #(.width(16)) adder_1 (.a(A), .b(B), .out(adder_1_out));  // open: cin, cout
  Subtractor #(.width(16)) subtractor_1 (.a(A), .b(B), .out(subtractor_1_out));  // open: bin, bout
  Multiplier #(.width(16)) multiplier_1 (.a(A), .b(B), .out(multiplier_1_out));  // open: cin, cout
  Divider #(.width(16)) divider_1 (.a(A), .b(B), .out(divider_1_out));  // open: upper, rem
  Register #(.width(3)) FLG_reg (.D(comparator_1_gt), .Q(FLG), .clk(CLK), .clr(RST));  // open: en
  Multiplexer #(.enable("true"), .select(2), .width(16)) multiplexer_1 (
    .in0(adder_1_out), .in1(subtractor_1_out), .in2(multiplier_1_out), .in3(divider_1_out), .out(BUS_O),
    .sel(ALM[1:0]), .en(and_1_out));
  and and_1 (and_1_out, ~ALM[2], ALO);  // AND_Gate
endmodule
